# Fritzing sketch bekotesi_terv_SPI (saved by Fritzing 0.9.3b)

parts:
  L298N1 = L298N DC motor driver
  M1 = DC Motor
  U1 = LIPO-2000mAh [package=lipo-2000]
  U2 = LIPO-2000mAh [package=lipo-2000]
  Part2 = Arduino Uno (Rev3) - ICSP
  Part3 = InvenSense MPU6050
  HC-SR04_Sensor_1 = HC-SR04 Ultrasonic Distance Sensor
  M2 = DC Motor
  HC-SR04_Sensor_2 = HC-SR04 Ultrasonic Distance Sensor
  HC-SR04_Sensor_3 = HC-SR04 Ultrasonic Distance Sensor
  Part4 = RFID-RC522-v3
  Boost_Convertor1 = Boost Convertor [part_number=XL6009E1 package=THT]

nets:
  N1: L298N1.OUT1, M2.pin_2
  N2: L298N1.OUT2, M2.pin_1
  N3: L298N1.OUT3, M1.pin_2
  N4: L298N1.OUT4, M1.pin_1
  VCC: L298N1.12V, Part3.VCC, HC-SR04_Sensor_1.VCC, HC-SR04_Sensor_2.VCC, HC-SR04_Sensor_3.VCC, Boost_Convertor1.Positive_Output
  GND: L298N1.GND, Part2.GND, Part3.GND, Part3.AD0, HC-SR04_Sensor_1.GND, HC-SR04_Sensor_2.GND, HC-SR04_Sensor_3.GND, Part4.GND, Boost_Convertor1.Negative_Output
  N5: L298N1.ENA, Part2.D6_PWM
  N6: L298N1.ENB, Part2.D5_PWM
  N7: L298N1.IN1, Part2.D8
  N8: L298N1.IN2, Part2.D7
  N9: L298N1.IN3, Part2.D4
  N10: L298N1.IN4, Part2.D3_PWM
  N11: U1.+, Boost_Convertor1.Positive_Input
  N12: U1.-, U2.+
  N13: U2.-, Boost_Convertor1.Negative_Input
  N14: Part2.A0, HC-SR04_Sensor_1.ECHO
  N15: Part2.A1, HC-SR04_Sensor_1.TRIG
  N16: Part2.A2, HC-SR04_Sensor_2.ECHO
  N17: Part2.A3, HC-SR04_Sensor_2.TRIG
  N18: Part2.A4/SDA, Part3.SDA, HC-SR04_Sensor_3.ECHO
  N19: Part2.A5/SCL, Part3.SCL, HC-SR04_Sensor_3.TRIG
  N20: Part2.ICSP_MISO, Part4.MISO
  N21: Part2.ICSP_SCK, Part4.SCK
  N22: Part2.ICSP_MOSI, Part4.MOSI
  N23: Part2.D9_PWM, Part4.IRQ
  N24: Part2.D2, Part4.SDA
  3V3: Part2.3V3, Part4.3.3V

notes:
  2 x 3.7 V LiPo Batteries connected in series
  Left Motor
  Right Motor
  L298N Motor Driver Board
  Left-side sensor
  Front sensor
  Right-side sensor
  XL6009-STEPUP set to 5V
  RFID with SPI

custom parts:
  L298N DC motor driver: 2x DC motor driver with 78M05 positive voltage regulator (7..35 V) L298N: max 46 V, 2 A Set 5 V Enable jumper to enable 5 V regultor (needed for the L298N) and +5 V output at screw terminal or supply external +5 V at screw terminal Set ENA and/or ENB to +5 V to enable motor permanently or supply ENA and/or ENB with PWM signal IN1 and IN2 set rotation directory for motor A (OUT1/OUT2) IN2 and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
  RFID-RC522-v3: A simple China made RFID-RC522 Reader (6x4 cm); do check the pin labels, as this is a MFRC522 based clone.
  Boost Convertor: DC to DC boost convertor
